// Digital circuit Registers_DRAM.dig as structural Verilog
module Registers_DRAM (
  input  CS,
  input  WE,
  input  OE,
  input  LD,
  input  INC,
  input  [3:0] JumpAddr_1,
  input  [3:0] JumpAddr_2,
  input  RST,
  input  clk,
  input  clk_2,
  input  [1:0] LD_2,
  input  RAM_OUT_EN,
  input  clk_3,
  input  [1:0] LD_3,
  input  CLR,
  input  ST,
  input  S_0,
  input  S_1,
  input  [3:0] I_0,
  input  [3:0] I_1,
  input  [3:0] I_2,
  input  [3:0] I_3,
  output [3:0] Output,
  output [3:0] Output_2
);

  wire [3:0] _4_bit_programcounter_1_pc, driver_1_out, Memory_d;

  _4_bit_ProgramCounter _4_bit_programcounter_1 (
    .LD(LD), .INC(INC), .JumpAddr_1(JumpAddr_1), .JumpAddr_2(JumpAddr_2), .clk(clk), .RST(RST),
    .PC(_4_bit_programcounter_1_pc));
  RAMSinglePortSel #(.AddrBits(4), .Bits(4)) Memory (
    .A(_4_bit_programcounter_1_pc), .CS(CS), .WE(WE), .OE(OE), .D(Memory_d));
  assign driver_1_out = RAM_OUT_EN ? Memory_d : 4'bz;  // Driver driver_1
  _4_bit_Register IR (.clk(clk_2), .Input(driver_1_out), .Write(LD_2), .\output (Output));
  GPR_Register_1 GPR (
    .clk(clk_3), .CLR(CLR), .ST(ST), .S0(S_0), .S1(S_1), .I_0(I_0), .I_1(I_1), .I_2(I_2), .I_3(I_3),
    .LD(LD_3), .Output(Output_2));
endmodule
